// Logisim project Atividade 9 Somador_Subtrador.circ as structural Verilog: 2 circuits, main circuit Sc
module Sc (
  input  in_1,
  input  in_2,
  input  in_3,
  output out_4,
  output out_5
);

  wire and_1_out, and_2_out, and_3_out, xor_1_out;

  and and_1 (and_1_out, in_1, in_2);
  and and_2 (and_2_out, in_1, in_3);
  or or_1 (out_4, and_1_out, and_2_out, and_3_out);
  and and_3 (and_3_out, in_2, in_3);
  xor xor_1 (xor_1_out, in_1, in_2);
  xor xor_2 (out_5, xor_1_out, in_3);
endmodule

module todos (
  input  in_1
);

  wire dipswitch_1_p1, dipswitch_1_p2, dipswitch_1_p3, dipswitch_1_p4, dipswitch_1_p5, dipswitch_1_p6,
       dipswitch_1_p7, dipswitch_1_p8, dipswitch_2_p1, dipswitch_2_p2, dipswitch_2_p3, dipswitch_2_p4,
       dipswitch_2_p5, dipswitch_2_p6, dipswitch_2_p7, dipswitch_2_p8, sc_1_out_4, sc_1_out_5, sc_2_out_4,
       sc_2_out_5, sc_3_out_4, sc_3_out_5, sc_4_out_4, sc_4_out_5, sc_5_out_4, sc_5_out_5, sc_6_out_4,
       sc_6_out_5, sc_7_out_4, sc_7_out_5, sc_8_out_4, sc_8_out_5, xor_1_out, xor_2_out, xor_3_out,
       xor_4_out, xor_5_out, xor_6_out, xor_7_out, xor_8_out;

  LED led_1 (.in(sc_1_out_4));
  Sc sc_1 (.out_4(sc_1_out_4), .out_5(sc_1_out_5), .in_1(sc_2_out_4), .in_2(dipswitch_1_p1), .in_3(xor_1_out));
  xor xor_1 (xor_1_out, in_1, dipswitch_2_p1);
  LED led_2 (.in(sc_1_out_5));
  xor xor_2 (xor_2_out, in_1, dipswitch_2_p2);
  Sc sc_2 (.out_4(sc_2_out_4), .out_5(sc_2_out_5), .in_1(sc_3_out_4), .in_2(dipswitch_1_p2), .in_3(xor_2_out));
  LED led_3 (.in(sc_2_out_5));
  Sc sc_3 (.out_4(sc_3_out_4), .out_5(sc_3_out_5), .in_1(sc_4_out_4), .in_2(dipswitch_1_p3), .in_3(xor_3_out));
  LED led_4 (.in(sc_3_out_5));
  // DipSwitch dipswitch_1: pin names not known; wires that end beside it: dipswitch_1_p1, dipswitch_1_p2, dipswitch_1_p3, dipswitch_1_p4, dipswitch_1_p5, dipswitch_1_p6, dipswitch_1_p7, dipswitch_1_p8
  xor xor_3 (xor_3_out, in_1, dipswitch_2_p3);
  Sc sc_4 (.out_4(sc_4_out_4), .out_5(sc_4_out_5), .in_1(sc_5_out_4), .in_2(dipswitch_1_p4), .in_3(xor_4_out));
  xor xor_4 (xor_4_out, in_1, dipswitch_2_p4);
  Sc sc_5 (.out_4(sc_5_out_4), .out_5(sc_5_out_5), .in_1(sc_6_out_4), .in_2(dipswitch_1_p5), .in_3(xor_5_out));
  LED led_5 (.in(sc_4_out_5));
  xor xor_5 (xor_5_out, in_1, dipswitch_2_p5);
  LED led_6 (.in(sc_5_out_5));
  xor xor_6 (xor_6_out, in_1, dipswitch_2_p6);
  Sc sc_6 (.out_4(sc_6_out_4), .out_5(sc_6_out_5), .in_1(sc_7_out_4), .in_2(dipswitch_1_p6), .in_3(xor_6_out));
  LED led_7 (.in(sc_6_out_5));
  // DipSwitch dipswitch_2: pin names not known; wires that end beside it: dipswitch_2_p1, dipswitch_2_p2, dipswitch_2_p3, dipswitch_2_p4, dipswitch_2_p5, dipswitch_2_p6, dipswitch_2_p7, dipswitch_2_p8
  Sc sc_7 (.out_4(sc_7_out_4), .out_5(sc_7_out_5), .in_1(sc_8_out_4), .in_2(dipswitch_1_p7), .in_3(xor_7_out));
  LED led_8 (.in(sc_7_out_5));
  xor xor_7 (xor_7_out, in_1, dipswitch_2_p7);
  Sc sc_8 (.out_4(sc_8_out_4), .out_5(sc_8_out_5), .in_1(in_1), .in_2(dipswitch_1_p8), .in_3(xor_8_out));
  LED led_9 (.in(sc_8_out_5));
  xor xor_8 (xor_8_out, in_1, dipswitch_2_p8);
endmodule
