// Logisim project Trabalho 2.circ as structural Verilog: 14 circuits, main circuit Porta1
module CircuitoFinal (
  input  [1:0] in_1,
  input  [1:0] in_2,
  input  [1:0] in_3,
  input  Sel,
  input  Escreve,
  input  [2:0] Sel_2
);

  wire demultiplexer_1_out0, demultiplexer_1_out1, demultiplexer_1_out2, demultiplexer_1_out3,
       todas_portas_1_out_18, todas_portas_1_out_20;
  wire [7:0] dipswitch_1_p8, multiplexer_1_out, multiplexer_2_out, multiplexer_3_out, r0_1_out_3, r1_1_out_3,
       r2_1_out_3, r3_1_out_3, todas_portas_1_out_19;

  Demultiplexer #(.enable("false"), .select(2)) demultiplexer_1 (
    .out0(demultiplexer_1_out0), .out1(demultiplexer_1_out1), .out2(demultiplexer_1_out2),
    .out3(demultiplexer_1_out3), .in(Escreve), .sel(in_1));
  Multiplexer #(.enable("false"), .width(8)) multiplexer_1 (
    .in0(todas_portas_1_out_19), .in1(dipswitch_1_p8), .out(multiplexer_1_out), .sel(Sel));
  R0 r0_1 (.out_3(r0_1_out_3), .in_1(multiplexer_1_out), .in_2(demultiplexer_1_out0));
  // DipSwitch dipswitch_1: pin names not known; wires that end beside it: dipswitch_1_p8[7], dipswitch_1_p8[6], dipswitch_1_p8[5], dipswitch_1_p8[4], dipswitch_1_p8[3], dipswitch_1_p8[2], dipswitch_1_p8[1], dipswitch_1_p8[0]
  R1 r1_1 (.out_3(r1_1_out_3), .in_1(multiplexer_1_out), .in_2(demultiplexer_1_out1));
  Multiplexer #(.enable("false"), .select(2), .width(8)) multiplexer_2 (
    .in0(r0_1_out_3), .in1(r1_1_out_3), .in2(r2_1_out_3), .in3(r3_1_out_3), .out(multiplexer_2_out),
    .sel(in_2));
  R2 r2_1 (.out_3(r2_1_out_3), .in_1(multiplexer_1_out), .in_2(demultiplexer_1_out2));
  LED led_1 (.in(todas_portas_1_out_20));
  LED led_2 (.in(todas_portas_1_out_18));
  R3 r3_1 (.out_3(r3_1_out_3), .in_1(multiplexer_1_out), .in_2(demultiplexer_1_out3));
  LED led_3 (.in(todas_portas_1_out_19[7]));
  LED led_4 (.in(todas_portas_1_out_19[6]));
  Multiplexer #(.enable("false"), .select(2), .width(8)) multiplexer_3 (
    .in0(r0_1_out_3), .in1(r1_1_out_3), .in2(r2_1_out_3), .in3(r3_1_out_3), .out(multiplexer_3_out),
    .sel(in_3));
  Todas_Portas todas_portas_1 (
    .out_19(todas_portas_1_out_19), .out_18(todas_portas_1_out_18), .out_20(todas_portas_1_out_20),
    .in_1(multiplexer_2_out[7]), .in_2(multiplexer_2_out[6]), .in_3(multiplexer_2_out[5]),
    .in_4(multiplexer_2_out[4]), .in_5(multiplexer_2_out[3]), .in_6(multiplexer_2_out[2]),
    .in_7(multiplexer_2_out[1]), .in_8(multiplexer_2_out[0]), .in_9(multiplexer_3_out[7]),
    .in_10(multiplexer_3_out[6]), .in_11(multiplexer_3_out[5]), .in_12(multiplexer_3_out[4]),
    .in_13(multiplexer_3_out[3]), .in_14(multiplexer_3_out[2]), .in_15(multiplexer_3_out[1]),
    .in_16(multiplexer_3_out[0]), .in_17(Sel_2));
  LED led_5 (.in(todas_portas_1_out_19[5]));
  LED led_6 (.in(todas_portas_1_out_19[4]));
  LED led_7 (.in(todas_portas_1_out_19[3]));
  LED led_8 (.in(todas_portas_1_out_19[2]));
  LED led_9 (.in(todas_portas_1_out_19[1]));
  LED led_10 (.in(todas_portas_1_out_19[0]));

  // Notes on the sheet:
  //   8
  //   Valor
  //   A
  //   Z
  //   C
  //   Sel.
  //   RW
  //   S
  //   Sel.
  //   RA
  //   B
  //   Sel.
  //   RB
  //   Op.
endmodule

module R0 (
  input  [7:0] in_1,
  input  in_2,
  output [7:0] out_3
);

  D_Flip_Flop d_ff_1 (.D(in_1[7]), .clk(in_2), .Q(out_3[7]));  // open: Qn, preset, reset
  D_Flip_Flop d_ff_2 (.D(in_1[6]), .clk(in_2), .Q(out_3[6]));  // open: Qn, preset, reset
  D_Flip_Flop d_ff_3 (.D(in_1[5]), .clk(in_2), .Q(out_3[5]));  // open: Qn, preset, reset
  D_Flip_Flop d_ff_4 (.D(in_1[4]), .clk(in_2), .Q(out_3[4]));  // open: Qn, preset, reset
  D_Flip_Flop d_ff_5 (.D(in_1[3]), .clk(in_2), .Q(out_3[3]));  // open: Qn, preset, reset
  D_Flip_Flop d_ff_6 (.D(in_1[2]), .clk(in_2), .Q(out_3[2]));  // open: Qn, preset, reset
  D_Flip_Flop d_ff_7 (.D(in_1[1]), .clk(in_2), .Q(out_3[1]));  // open: Qn, preset, reset
  D_Flip_Flop d_ff_8 (.D(in_1[0]), .clk(in_2), .Q(out_3[0]));  // open: Qn, preset, reset
endmodule

module R1 (
  input  [7:0] in_1,
  input  in_2,
  output [7:0] out_3
);

  D_Flip_Flop d_ff_1 (.D(in_1[7]), .clk(in_2), .Q(out_3[7]));  // open: Qn, preset, reset
  D_Flip_Flop d_ff_2 (.D(in_1[6]), .clk(in_2), .Q(out_3[6]));  // open: Qn, preset, reset
  D_Flip_Flop d_ff_3 (.D(in_1[5]), .clk(in_2), .Q(out_3[5]));  // open: Qn, preset, reset
  D_Flip_Flop d_ff_4 (.D(in_1[4]), .clk(in_2), .Q(out_3[4]));  // open: Qn, preset, reset
  D_Flip_Flop d_ff_5 (.D(in_1[3]), .clk(in_2), .Q(out_3[3]));  // open: Qn, preset, reset
  D_Flip_Flop d_ff_6 (.D(in_1[2]), .clk(in_2), .Q(out_3[2]));  // open: Qn, preset, reset
  D_Flip_Flop d_ff_7 (.D(in_1[1]), .clk(in_2), .Q(out_3[1]));  // open: Qn, preset, reset
  D_Flip_Flop d_ff_8 (.D(in_1[0]), .clk(in_2), .Q(out_3[0]));  // open: Qn, preset, reset
endmodule

module R2 (
  input  [7:0] in_1,
  input  in_2,
  output [7:0] out_3
);

  D_Flip_Flop d_ff_1 (.D(in_1[7]), .clk(in_2), .Q(out_3[7]));  // open: Qn, preset, reset
  D_Flip_Flop d_ff_2 (.D(in_1[6]), .clk(in_2), .Q(out_3[6]));  // open: Qn, preset, reset
  D_Flip_Flop d_ff_3 (.D(in_1[5]), .clk(in_2), .Q(out_3[5]));  // open: Qn, preset, reset
  D_Flip_Flop d_ff_4 (.D(in_1[4]), .clk(in_2), .Q(out_3[4]));  // open: Qn, preset, reset
  D_Flip_Flop d_ff_5 (.D(in_1[3]), .clk(in_2), .Q(out_3[3]));  // open: Qn, preset, reset
  D_Flip_Flop d_ff_6 (.D(in_1[2]), .clk(in_2), .Q(out_3[2]));  // open: Qn, preset, reset
  D_Flip_Flop d_ff_7 (.D(in_1[1]), .clk(in_2), .Q(out_3[1]));  // open: Qn, preset, reset
  D_Flip_Flop d_ff_8 (.D(in_1[0]), .clk(in_2), .Q(out_3[0]));  // open: Qn, preset, reset
endmodule

module R3 (
  input  [7:0] in_1,
  input  in_2,
  output [7:0] out_3
);

  D_Flip_Flop d_ff_1 (.D(in_1[7]), .clk(in_2), .Q(out_3[7]));  // open: Qn, preset, reset
  D_Flip_Flop d_ff_2 (.D(in_1[6]), .clk(in_2), .Q(out_3[6]));  // open: Qn, preset, reset
  D_Flip_Flop d_ff_3 (.D(in_1[5]), .clk(in_2), .Q(out_3[5]));  // open: Qn, preset, reset
  D_Flip_Flop d_ff_4 (.D(in_1[4]), .clk(in_2), .Q(out_3[4]));  // open: Qn, preset, reset
  D_Flip_Flop d_ff_5 (.D(in_1[3]), .clk(in_2), .Q(out_3[3]));  // open: Qn, preset, reset
  D_Flip_Flop d_ff_6 (.D(in_1[2]), .clk(in_2), .Q(out_3[2]));  // open: Qn, preset, reset
  D_Flip_Flop d_ff_7 (.D(in_1[1]), .clk(in_2), .Q(out_3[1]));  // open: Qn, preset, reset
  D_Flip_Flop d_ff_8 (.D(in_1[0]), .clk(in_2), .Q(out_3[0]));  // open: Qn, preset, reset
endmodule

module Todas_Portas (
  input  in_1,
  input  in_2,
  input  in_3,
  input  in_4,
  input  in_5,
  input  in_6,
  input  in_7,
  input  in_8,
  input  in_9,
  input  in_10,
  input  in_11,
  input  in_12,
  input  in_13,
  input  in_14,
  input  in_15,
  input  in_16,
  input  [2:0] in_17,
  output out_18,
  output [7:0] out_19,
  output out_20
);

  wire [7:0] not_1_out, porta1_1_1_out_25, porta2_1_out_24, porta3_1_out_24, porta4_1_out_24,
       porta5_1_out_16, porta6_1_out_24, porta8_1_out_24;

  porta1_1 porta1_1_1 (
    .out_17(out_18), .out_18(porta1_1_1_out_25[7]), .out_19(porta1_1_1_out_25[6]),
    .out_20(porta1_1_1_out_25[5]), .out_21(porta1_1_1_out_25[4]), .out_22(porta1_1_1_out_25[3]),
    .out_23(porta1_1_1_out_25[2]), .out_24(porta1_1_1_out_25[1]), .out_25(porta1_1_1_out_25[0]), .in_1(in_1),
    .in_2(in_2), .in_3(in_3), .in_4(in_4), .in_5(in_5), .in_6(in_6), .in_7(in_7), .in_8(in_8), .in_9(in_9),
    .in_10(in_10), .in_11(in_11), .in_12(in_12), .in_13(in_13), .in_14(in_14), .in_15(in_15), .in_16(in_16));
  Porta2 porta2_1 (
    .out_17(porta2_1_out_24[7]), .out_18(porta2_1_out_24[6]), .out_19(porta2_1_out_24[5]),
    .out_20(porta2_1_out_24[4]), .out_21(porta2_1_out_24[3]), .out_22(porta2_1_out_24[2]),
    .out_23(porta2_1_out_24[1]), .out_24(porta2_1_out_24[0]), .in_1(in_1), .in_2(in_2), .in_3(in_3),
    .in_4(in_4), .in_5(in_5), .in_6(in_6), .in_7(in_7), .in_8(in_8), .in_9(in_9), .in_10(in_10),
    .in_11(in_11), .in_12(in_12), .in_13(in_13), .in_14(in_14), .in_15(in_15), .in_16(in_16));
  Porta3 porta3_1 (
    .out_17(porta3_1_out_24[7]), .out_18(porta3_1_out_24[6]), .out_19(porta3_1_out_24[5]),
    .out_20(porta3_1_out_24[4]), .out_21(porta3_1_out_24[3]), .out_22(porta3_1_out_24[2]),
    .out_23(porta3_1_out_24[1]), .out_24(porta3_1_out_24[0]), .in_1(in_1), .in_2(in_2), .in_3(in_3),
    .in_4(in_4), .in_5(in_5), .in_6(in_6), .in_7(in_7), .in_8(in_8), .in_9(in_9), .in_10(in_10),
    .in_11(in_11), .in_12(in_12), .in_13(in_13), .in_14(in_14), .in_15(in_15), .in_16(in_16));
  assign not_1_out = ~out_19;  // NOT_Gate not_1, 8 bits wide
  or or_1 (out_20, not_1_out[7], not_1_out[6], not_1_out[5], not_1_out[4], not_1_out[3], not_1_out[2], not_1_out[1], not_1_out[0]);
  Porta4 porta4_1 (
    .out_17(porta4_1_out_24[7]), .out_18(porta4_1_out_24[6]), .out_19(porta4_1_out_24[5]),
    .out_20(porta4_1_out_24[4]), .out_21(porta4_1_out_24[3]), .out_22(porta4_1_out_24[2]),
    .out_23(porta4_1_out_24[1]), .out_24(porta4_1_out_24[0]), .in_1(in_1), .in_2(in_2), .in_3(in_3),
    .in_4(in_4), .in_5(in_5), .in_6(in_6), .in_7(in_7), .in_8(in_8), .in_9(in_9), .in_10(in_10),
    .in_11(in_11), .in_12(in_12), .in_13(in_13), .in_14(in_14), .in_15(in_15), .in_16(in_16));
  Multiplexer #(.disabled("Z"), .enable("false"), .select(3), .width(8)) multiplexer_1 (
    .in0(porta1_1_1_out_25), .in1(porta2_1_out_24), .in2(porta3_1_out_24), .in3(porta4_1_out_24),
    .in4(porta5_1_out_16), .in5(porta6_1_out_24),
    .in6({in_9, in_10, in_11, in_12, in_13, in_14, in_15, in_16}), .in7(porta8_1_out_24), .out(out_19),
    .sel(in_17));
  Porta5 porta5_1 (
    .out_9(porta5_1_out_16[7]), .out_10(porta5_1_out_16[6]), .out_11(porta5_1_out_16[5]),
    .out_12(porta5_1_out_16[4]), .out_13(porta5_1_out_16[3]), .out_14(porta5_1_out_16[2]),
    .out_15(porta5_1_out_16[1]), .out_16(porta5_1_out_16[0]), .in_1(in_1), .in_2(in_2), .in_3(in_3),
    .in_4(in_4), .in_5(in_5), .in_6(in_6), .in_7(in_7), .in_8(in_8));
  Porta6 porta6_1 (
    .out_17(porta6_1_out_24[7]), .out_18(porta6_1_out_24[6]), .out_19(porta6_1_out_24[5]),
    .out_20(porta6_1_out_24[4]), .out_21(porta6_1_out_24[3]), .out_22(porta6_1_out_24[2]),
    .out_23(porta6_1_out_24[1]), .out_24(porta6_1_out_24[0]), .in_1(in_1), .in_2(in_2), .in_3(in_3),
    .in_4(in_4), .in_5(in_5), .in_6(in_6), .in_7(in_7), .in_8(in_8), .in_9(in_9), .in_10(in_10),
    .in_11(in_11), .in_12(in_12), .in_13(in_13), .in_14(in_14), .in_15(in_15), .in_16(in_16));
  Porta8 porta8_1 (
    .out_17(porta8_1_out_24[7]), .out_18(porta8_1_out_24[6]), .out_19(porta8_1_out_24[5]),
    .out_20(porta8_1_out_24[4]), .out_21(porta8_1_out_24[3]), .out_22(porta8_1_out_24[2]),
    .out_23(porta8_1_out_24[1]), .out_24(porta8_1_out_24[0]), .in_1(in_1), .in_2(in_2), .in_3(in_3),
    .in_4(in_4), .in_5(in_5), .in_6(in_6), .in_7(in_7), .in_8(in_8), .in_9(in_9), .in_10(in_10),
    .in_11(in_11), .in_12(in_12), .in_13(in_13), .in_14(in_14), .in_15(in_15), .in_16(in_16));
endmodule

module Porta1 (
  input  in_1,
  input  in_2,
  input  in_3,
  output out_4,
  output out_5
);

  wire and_1_out, and_2_out, and_3_out, xor_1_out;

  and and_1 (and_1_out, in_2, in_3);
  and and_2 (and_2_out, in_1, in_3);
  or or_1 (out_5, and_1_out, and_2_out, and_3_out);
  and and_3 (and_3_out, in_1, in_2);
  xor xor_1 (xor_1_out, in_1, in_2);
  xor xor_2 (out_4, xor_1_out, in_3);
endmodule

module porta1_1 (
  input  in_1,
  input  in_2,
  input  in_3,
  input  in_4,
  input  in_5,
  input  in_6,
  input  in_7,
  input  in_8,
  input  in_9,
  input  in_10,
  input  in_11,
  input  in_12,
  input  in_13,
  input  in_14,
  input  in_15,
  input  in_16,
  output out_17,
  output out_18,
  output out_19,
  output out_20,
  output out_21,
  output out_22,
  output out_23,
  output out_24,
  output out_25
);

  wire porta1_2_out_5, porta1_3_out_5, porta1_4_out_5, porta1_5_out_5, porta1_6_out_5, porta1_7_out_5,
       porta1_8_out_5;

  Porta1 porta1_1 (.out_5(out_17), .out_4(out_18), .in_1(in_1), .in_2(in_9), .in_3(porta1_2_out_5));
  Porta1 porta1_2 (.out_5(porta1_2_out_5), .out_4(out_19), .in_1(in_2), .in_2(in_10), .in_3(porta1_3_out_5));
  Porta1 porta1_3 (.out_5(porta1_3_out_5), .out_4(out_20), .in_1(in_3), .in_2(in_11), .in_3(porta1_4_out_5));
  Porta1 porta1_4 (.out_5(porta1_4_out_5), .out_4(out_21), .in_1(in_4), .in_2(in_12), .in_3(porta1_5_out_5));
  Porta1 porta1_5 (.out_5(porta1_5_out_5), .out_4(out_22), .in_1(in_5), .in_2(in_13), .in_3(porta1_6_out_5));
  Porta1 porta1_6 (.out_5(porta1_6_out_5), .out_4(out_23), .in_1(in_6), .in_2(in_14), .in_3(porta1_7_out_5));
  Porta1 porta1_7 (.out_5(porta1_7_out_5), .out_4(out_24), .in_1(in_7), .in_2(in_15), .in_3(porta1_8_out_5));
  Porta1 porta1_8 (.out_5(porta1_8_out_5), .out_4(out_25), .in_1(in_8), .in_2(in_16), .in_3(1'b0));
endmodule

module Porta2 (
  input  in_1,
  input  in_2,
  input  in_3,
  input  in_4,
  input  in_5,
  input  in_6,
  input  in_7,
  input  in_8,
  input  in_9,
  input  in_10,
  input  in_11,
  input  in_12,
  input  in_13,
  input  in_14,
  input  in_15,
  input  in_16,
  output out_17,
  output out_18,
  output out_19,
  output out_20,
  output out_21,
  output out_22,
  output out_23,
  output out_24
);

  or or_1 (out_17, in_1, in_9);
  or or_2 (out_18, in_2, in_10);
  or or_3 (out_19, in_3, in_11);
  or or_4 (out_20, in_4, in_12);
  or or_5 (out_21, in_5, in_13);
  or or_6 (out_22, in_6, in_14);
  or or_7 (out_23, in_7, in_15);
  or or_8 (out_24, in_8, in_16);
endmodule

module Porta3 (
  input  in_1,
  input  in_2,
  input  in_3,
  input  in_4,
  input  in_5,
  input  in_6,
  input  in_7,
  input  in_8,
  input  in_9,
  input  in_10,
  input  in_11,
  input  in_12,
  input  in_13,
  input  in_14,
  input  in_15,
  input  in_16,
  output out_17,
  output out_18,
  output out_19,
  output out_20,
  output out_21,
  output out_22,
  output out_23,
  output out_24
);

  nor nor_1 (out_17, in_1, in_9);
  nor nor_2 (out_18, in_2, in_10);
  nor nor_3 (out_19, in_3, in_11);
  nor nor_4 (out_20, in_4, in_12);
  nor nor_5 (out_21, in_5, in_13);
  nor nor_6 (out_22, in_6, in_14);
  nor nor_7 (out_23, in_7, in_15);
  nor nor_8 (out_24, in_8, in_16);
endmodule

module Porta4 (
  input  in_1,
  input  in_2,
  input  in_3,
  input  in_4,
  input  in_5,
  input  in_6,
  input  in_7,
  input  in_8,
  input  in_9,
  input  in_10,
  input  in_11,
  input  in_12,
  input  in_13,
  input  in_14,
  input  in_15,
  input  in_16,
  output out_17,
  output out_18,
  output out_19,
  output out_20,
  output out_21,
  output out_22,
  output out_23,
  output out_24
);

  and and_1 (out_17, in_1, in_9);
  and and_2 (out_18, in_2, in_10);
  and and_3 (out_19, in_3, in_11);
  and and_4 (out_20, in_4, in_12);
  and and_5 (out_21, in_5, in_13);
  and and_6 (out_22, in_6, in_14);
  and and_7 (out_23, in_7, in_15);
  and and_8 (out_24, in_8, in_16);
endmodule

module Porta5 (
  input  in_1,
  input  in_2,
  input  in_3,
  input  in_4,
  input  in_5,
  input  in_6,
  input  in_7,
  input  in_8,
  output out_9,
  output out_10,
  output out_11,
  output out_12,
  output out_13,
  output out_14,
  output out_15,
  output out_16
);

  not not_1 (out_9, in_1);
  not not_2 (out_10, in_2);
  not not_3 (out_11, in_3);
  not not_4 (out_12, in_4);
  not not_5 (out_13, in_5);
  not not_6 (out_14, in_6);
  not not_7 (out_15, in_7);
  not not_8 (out_16, in_8);
endmodule

module Porta6 (
  input  in_1,
  input  in_2,
  input  in_3,
  input  in_4,
  input  in_5,
  input  in_6,
  input  in_7,
  input  in_8,
  input  in_9,
  input  in_10,
  input  in_11,
  input  in_12,
  input  in_13,
  input  in_14,
  input  in_15,
  input  in_16,
  output out_17,
  output out_18,
  output out_19,
  output out_20,
  output out_21,
  output out_22,
  output out_23,
  output out_24
);

  wire not_1_out, not_2_out, not_3_out, not_4_out, not_5_out, not_6_out, not_7_out, not_8_out, not_9_out,
       not_10_out, not_11_out, not_12_out, not_13_out, not_14_out, not_15_out, not_16_out;

  not not_1 (not_1_out, in_1);
  not not_2 (not_2_out, in_2);
  not not_3 (not_3_out, in_3);
  not not_4 (not_4_out, in_4);
  xor xor_1 (out_17, not_1_out, not_9_out);
  not not_5 (not_5_out, in_5);
  not not_6 (not_6_out, in_6);
  xor xor_2 (out_18, not_2_out, not_10_out);
  not not_7 (not_7_out, in_7);
  not not_8 (not_8_out, in_8);
  xor xor_3 (out_19, not_3_out, not_11_out);
  xor xor_4 (out_20, not_4_out, not_12_out);
  not not_9 (not_9_out, in_9);
  xor xor_5 (out_21, not_5_out, not_13_out);
  not not_10 (not_10_out, in_10);
  not not_11 (not_11_out, in_11);
  xor xor_6 (out_22, not_6_out, not_14_out);
  xor xor_7 (out_23, not_7_out, not_15_out);
  not not_12 (not_12_out, in_12);
  not not_13 (not_13_out, in_13);
  xor xor_8 (out_24, not_8_out, not_16_out);
  not not_14 (not_14_out, in_14);
  not not_15 (not_15_out, in_15);
  not not_16 (not_16_out, in_16);
endmodule

module Porta8 (
  input  in_1,
  input  in_2,
  input  in_3,
  input  in_4,
  input  in_5,
  input  in_6,
  input  in_7,
  input  in_8,
  input  in_9,
  input  in_10,
  input  in_11,
  input  in_12,
  input  in_13,
  input  in_14,
  input  in_15,
  input  in_16,
  output out_17,
  output out_18,
  output out_19,
  output out_20,
  output out_21,
  output out_22,
  output out_23,
  output out_24
);

  nand nand_1 (out_17, in_1, in_9);
  nand nand_2 (out_18, in_2, in_10);
  nand nand_3 (out_19, in_3, in_11);
  nand nand_4 (out_20, in_4, in_12);
  nand nand_5 (out_21, in_5, in_13);
  nand nand_6 (out_22, in_6, in_14);
  nand nand_7 (out_23, in_7, in_15);
  nand nand_8 (out_24, in_8, in_16);
endmodule
